# Fritzing sketch Circuit (saved by Fritzing 0.9.3b)
breadboards: 2

parts:
  U1 = ESP32-38PinWide [part_number=ESP32-38PinWide]
  R1 = Photocell (LDR) [package=THT]
  LED1 = LED - 5mm [color="Red (633nm)" package="5 mm [THT]"]
  LED2 = LED - 5mm [color="Green (555nm)" package="5 mm [THT]"]
  R2 = Resistor [tolerance=±5% resistance=220 package="2512 [SMD]"]
  R3 = Resistor [tolerance=±5% resistance=220 package="2512 [SMD]"]
  R4 = Resistor [tolerance=±5% resistance=220 package="2512 [SMD]"]
  S1 = Pushbutton [package="[SMD]"]
  AM1 = AM2320 Humidity and Temperature Sensor [part_number="Adafruit #3721"]
  R5 = Resistor [tolerance=±5% resistance=2.2k package="2512 [SMD]"]
  R6 = Resistor [tolerance=±5% resistance=2.2k package="2512 [SMD]"]
  J2 = Dagu DGServo 9g header (male) [package=THT]

nets:
  N1: U1.GPIO21, AM1.SDA, R6.Pin_0
  N2: U1.GPIO22, AM1.SCL, R5.Pin_0
  N3: R1.pin_0, R4.Pin_1
  VDD: R1.pin_1, S1.Pin_1, S1.Pin_2, AM1.VDD, R5.Pin_1, R6.Pin_1, J2.Vcc
  GND: LED1.cathode, LED2.cathode, R4.Pin_0, AM1.GND, J2.gnd
  N4: LED1.anode, R3.Pin_0
  N5: LED2.anode, R2.Pin_0
  N6: S1.Pin_3, S1.Pin_4

notes:
  KYTO2800D

custom parts:
  ESP32-38PinWide: Generic 38-Pin ESP32 with wide format (only access to one side of pins on a breadboard) based on Stephen Lilley's HiLetgo ESP-WROOM-32 ESP32 ESP-32S Development Board.
  AM2320 Humidity and Temperature Sensor: AM2320 I2C Humidity and Temperature Sensor
